# Fritzing sketch tempwiringdiagram (saved by Fritzing 0.9.2b)
breadboards: 1

parts:
  Part1 = Arduino Pro Mini v13
  U1 = TMP36 [package=to-92-kit]
  C1 = Ceramic Capacitor [capacitance=100nF package="100 mil [THT, multilayer]"]

nets:
  GND: Part1.GND, U1.GND, C1.1
  N1: Part1.RESET, U1.VCC
  N2: Part1.A0, U1.VOUT, C1.0
